// Logisim project brainprocessor.circ as structural Verilog: 1 circuit, main circuit main
module main (
);

  wire and_1_out, and_3_out, and_4_out, and_5_out, and_6_out, and_7_out, and_8_out, and_9_out, and_10_out,
       and_12_out, and_13_out, and_14_out, Clock_out, comparator_1_eq, comparator_2_eq, comparator_3_eq,
       comparator_4_eq, comparator_5_eq, comparator_6_eq, comparator_7_eq, comparator_8_eq, comparator_9_eq,
       comparator_10_eq, comparator_11_eq, comparator_12_eq, demultiplexer_1_out0, demultiplexer_1_out1,
       demultiplexer_2_out0, demultiplexer_2_out1, demultiplexer_3_out0, demultiplexer_3_out1,
       keyboard_1_avail, nor_1_out, nor_2_out, nor_3_out, not_1_out, not_2_out, not_3_out, or_1_out,
       or_2_out, or_3_out, or_4_out, or_5_out, or_6_out, or_7_out, or_11_out, Reset_out;
  wire [4:0] FSM_q, not_4_out;
  wire [6:0] bit_extender_2_out, keyboard_1_data;
  wire [7:0] and_2_out, bit_extender_1_out, bit_extender_3_out, BUF_q, multiplexer_1_out, ram_1_data,
       rom_1_data;
  wire [11:0] AR_q, BRAC_q, PC_q;

  Clock Clock (.out(Clock_out));
  Button Reset (.out(Reset_out));
  not not_1 (not_1_out, comparator_9_eq);
  and and_1 (and_1_out, not_1_out, nor_1_out);
  Counter #(.width(12), .max('hfff)) PC (
    .load(not_4_out[2]), .count(and_1_out), .Q(PC_q), .clk(Clock_out), .clr(Reset_out));  // open: D, carry
  Comparator comparator_1 (.a(and_2_out), .b(8'h2c), .eq(comparator_1_eq));  // open: gt, lt
  Comparator comparator_2 (.a(and_2_out), .b(8'h2e), .eq(comparator_2_eq));  // open: gt, lt
  Comparator comparator_3 (.a(rom_1_data), .b(8'h5b), .eq(comparator_3_eq));  // open: gt, lt
  Comparator comparator_4 (.a(rom_1_data), .b(8'h5d), .eq(comparator_4_eq));  // open: gt, lt
  Counter #(.width(12), .max('hfff)) BRAC (
    .load(or_2_out), .count(or_1_out), .Q(BRAC_q), .clk(Clock_out), .clr(Reset_out));  // open: D, carry
  not not_2 (not_2_out, FSM_q[0]);
  Register #(.width(5)) FSM (.D(not_4_out), .Q(FSM_q), .clk(Clock_out), .clr(Reset_out));  // open: en
  or or_1 (or_1_out, or_2_out, or_3_out, or_11_out);
  nor nor_1 (nor_1_out, FSM_q[3], and_14_out, not_2_out);
  or or_2 (or_2_out, and_3_out, and_4_out);
  or or_3 (or_3_out, and_5_out, and_6_out);
  ROM #(.addrWidth(12)) rom_1 (.addr(PC_q), .data(rom_1_data));  // open: sel
  assign and_2_out = rom_1_data & bit_extender_1_out;  // AND_Gate and_2, 8 bits wide
  Comparator comparator_5 (.a(and_2_out), .b(8'h3c), .eq(comparator_5_eq));  // open: gt, lt
  Comparator comparator_6 (.a(and_2_out), .b(8'h3e), .eq(comparator_6_eq));  // open: gt, lt
  Comparator comparator_7 (.a(and_2_out), .b(8'h2d), .eq(comparator_7_eq));  // open: gt, lt
  Comparator comparator_8 (.a(and_2_out), .b(8'h2b), .eq(comparator_8_eq));  // open: gt, lt
  and and_3 (and_3_out, FSM_q[1], comparator_4_eq);
  and and_4 (and_4_out, FSM_q[2], comparator_3_eq);
  and and_5 (and_5_out, FSM_q[1], comparator_3_eq);
  and and_6 (and_6_out, FSM_q[2], comparator_4_eq);
  Comparator comparator_9 (.a({8{1'b0}}), .b(rom_1_data), .eq(comparator_9_eq));  // open: gt, lt
  assign bit_extender_1_out = {{7{FSM_q[4]}}, FSM_q[4]};  // Bit_Extender bit_extender_1
  Counter #(.width(12), .max('hfff)) AR (
    .load(comparator_5_eq), .count(or_4_out), .Q(AR_q), .clk(Clock_out), .clr(Reset_out));  // open: D, carry
  or or_4 (or_4_out, or_5_out, not_2_out);
  or or_5 (or_5_out, comparator_5_eq, comparator_6_eq);
  not not_3 (not_3_out, Clock_out);
  or or_6 (or_6_out, FSM_q[3], comparator_1_eq, comparator_7_eq);
  or or_7 (or_7_out, comparator_7_eq, comparator_8_eq);
  nor nor_2 (nor_2_out, FSM_q[3], not_2_out);
  and and_7 (and_7_out, comparator_3_eq, comparator_12_eq);
  and and_8 (and_8_out, comparator_4_eq, ~comparator_12_eq);  // AND_Gate
  Counter BUF (
    .load(or_6_out), .D(multiplexer_1_out), .count(or_7_out), .Q(BUF_q), .clk(Clock_out), .clr(Reset_out));  // open: carry
  Comparator #(.width(12)) comparator_10 (.a(BRAC_q), .b(12'h1), .eq(comparator_10_eq));  // open: gt, lt
  and and_9 (and_9_out, comparator_10_eq, or_2_out);
  Demultiplexer #(.disabled(0), .enable("false")) demultiplexer_1 (
    .out0(demultiplexer_1_out0), .out1(demultiplexer_1_out1), .in(not_2_out), .sel(comparator_11_eq));
  Demultiplexer #(.disabled(0), .enable("false")) demultiplexer_2 (
    .out0(demultiplexer_2_out0), .out1(demultiplexer_2_out1), .in(FSM_q[1]), .sel(and_9_out));
  Demultiplexer #(.disabled(0), .enable("false")) demultiplexer_3 (
    .out0(demultiplexer_3_out0), .out1(demultiplexer_3_out1), .in(FSM_q[2]), .sel(and_9_out));
  RAM #(.addrWidth(12), .bus("asynch")) ram_1 (
    .addr(AR_q), .data(ram_1_data), .sel(not_3_out), .ld(FSM_q[3]));  // open: clr
  assign ram_1_data = nor_2_out ? BUF_q : 8'bz;  // Controlled_Buffer controlled_buffer_1
  assign ram_1_data = not_2_out ? {8{1'b0}} : 8'bz;  // Controlled_Buffer controlled_buffer_2
  Multiplexer #(.width(8), .enable("false")) multiplexer_1 (
    .in0(ram_1_data), .in1(bit_extender_3_out), .out(multiplexer_1_out), .sel(comparator_1_eq));
  Comparator #(.width(12)) comparator_11 (.a(AR_q), .b({12{1'b1}}), .eq(comparator_11_eq));  // open: gt, lt
  and and_10 (and_10_out, FSM_q[4], nor_3_out);
  nor nor_3 (nor_3_out, or_5_out, and_7_out, and_8_out);
  and and_11 (not_4_out[3], FSM_q[4], or_5_out);
  and and_12 (and_12_out, FSM_q[4], and_7_out);
  and and_13 (and_13_out, FSM_q[4], and_8_out);
  Bit_Extender #(.out_width(7)) bit_extender_2 (.in(ram_1_data), .out(bit_extender_2_out));
  TTY tty_1 (.data(bit_extender_2_out), .clk(Clock_out), .we(comparator_2_eq), .clr(Reset_out));
  Keyboard keyboard_1 (
    .clk(Clock_out), .re(comparator_1_eq), .clr(Reset_out), .avail(keyboard_1_avail), .data(keyboard_1_data));
  Comparator comparator_12 (.a(BUF_q), .b({8{1'b0}}), .eq(comparator_12_eq));  // open: gt, lt
  or or_8 (not_4_out[1], demultiplexer_2_out0, and_12_out);
  or or_9 (not_4_out[2], demultiplexer_3_out0, and_13_out);
  or or_10 (not_4_out[4], demultiplexer_1_out1, demultiplexer_2_out1, demultiplexer_3_out1, FSM_q[3], and_10_out);
  or or_11 (or_11_out, and_12_out, and_13_out);
  and and_14 (and_14_out, ~keyboard_1_avail, comparator_1_eq);  // AND_Gate
  assign bit_extender_3_out = {{1{1'b0}}, keyboard_1_data};  // Bit_Extender bit_extender_3
  not not_4 (not_4_out[0], demultiplexer_1_out0);

  // Notes on the sheet:
  //   ,
  //   .
  //   [
  //   ]
  //   Clear RAM
  //   Skip forward
  //   Skip backward
  //   Load
  //   Run
  //   contents of rom_1 (hex, n*v repeats v):
  //   a 5b 54 68 69 73 20 70 72 6f 67 72 61 6d 20 70 72 69 6e 74 73 20 22 48 65 6c 6c 6f 2c 20 57 6f 72 6c
  //   64 21 22 5d a a 9*2b 5b 3e 8*2b 3c 2d 5d 3e 2e 3c 11*20 39 78 38 3d 37 32 10*20 48 a 9*2b 5b 3e 2b
  //   2b 2b 3c 2d 5d 3e 2b 2b 2e 15*20 37 32 70 39 78 33 70 32 3d 31 30 31 4*20 65 a 7*2b 2e 2e 27*20 31
  //   30 31 70 37 3d 31 30 38 7*20 6c 20 6c a 2b 2b 2b 2e 32*20 31 30 38 70 33 3d 31 31 31 7*20 6f a 3e
  //   5*2b 5b 3e 8*2b 3c 2d 5d 3e 4*2b 2e 11*20 35 78 38 70 34 3d 34 34 8*20 63 6f 6d 6d 61 a 3e 2b 2b 5b
  //   3c 6*2d 3e 2d 5d 3c 2e 20*20 34 34 6d 32 78 36 3d 33 32 7*20 73 70 61 63 65 a 3e 7*2b 5b 3e 6*2b 3c
  //   2d 5d 3e 5b 2d 3c 2b 2b 3e 5d 3c 2b 2b 2b 2e 4*20 37 78 36 78 32 70 33 3d 38 37 6*20 57 a 3c 3c 3c
  //   2e 48*20 6f a 2b 2b 2b 2e 32*20 31 31 31 70 33 3d 31 31 34 7*20 72 a 6*2d 2e 29*20 31 31 34 6d 36 3d
  //   31 30 38 7*20 6c a 8*2d 2e 27*20 31 30 38 6d 38 3d 31 30 30 7*20 64 a 3e 3e 2b 2e 32*20 33 32 70 31
  //   3d 33 33 9*20 65 78 63 6c 61 69 6d a
  //   <
  //   >
  //   -
  //   +
endmodule
